# Fritzing sketch Linda (saved by Fritzing 0.9.3b)

parts:
  Display1 = LCD screen 16x2 IIC [part_number=101290]
  Part1 = RFID-RC522-v2
  Keypad4x2 = Keypad Membran 4x4
  Part2 = Arduino Uno (Rev3)
  KY-1 = Keyes Relay [package=THT]
  J1 = Piezo Speaker
  U1 = ESP32-38PinWide [part_number=ESP32-38PinWide]
  L1 = Solenoid

nets:
  GND: Display1.GND, Part1.GND, Part2.GND, KY-1.ground, J1.pin1, U1.GND
  VCC: Display1.VCC, Part2.D7, Part2.5V, KY-1.signal, KY-1.power
  N1: Display1.SDA, Part2.A4/SDA
  N2: Display1.SCL, Part1.SDA, Part2.A5/SCL
  N3: Part1.SCK, Part2.D13/SCK
  N4: Part1.MOSI, Part2.D11_PWM/MOSI
  N5: Part1.MISO, Part2.D12/MISO
  N6: Part1.RST, Part2.D9_PWM
  3.3V: Part1.3.3V, Part2.3V3
  N7: Keypad4x2.Pin1, Part2.A0
  N8: Keypad4x2.Pin2, Part2.A1
  N9: Keypad4x2.Pin3, Part2.A2
  N10: Keypad4x2.Pin4, Part2.A3
  N11: Keypad4x2.Pin5, Part2.D5_PWM
  N12: Keypad4x2.Pin6, Part2.D4
  N13: Keypad4x2.Pin7, Part2.D3_PWM
  N14: Keypad4x2.Pin8, Part2.D2
  N15: Part2.D8, J1.pin2
  N16: Part2.D0/RX, U1.GPIO17
  N17: Part2.D1/TX, U1.GPIO16
  N18: KY-1.C, L1.pin2

notes:
  POWER SUPPLY 12 VOLT

custom parts:
  LCD screen 16x2 IIC: LCD screen with HD44780 controller enables showing text, symbols, value or anything else that comes from Croduino/Arduino. It is capable of showing 16 symbols in two lines and therefore can be used in many projects that need to send clearly visible and legible output information.. • Color of symbols: White • Backlight: Blue • Dimensions: 80 x 36 x 12 mm • Screen dimensions: 64.5 x 16 mm •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
  RFID-RC522-v2: A simple China made RFID-RC522 Reader; do check the pin labels, as this is a MFRC522 based clone.
  Keypad Membran 4x4: Membrane Keypad 4x4 Matrix
  Keyes Relay: The Keyes 5V relay module is suitable for SCM development, home appliance control. It uses a 5V~12V TIL control signal which can control DC / AC signal.
  ESP32-38PinWide: Generic 38-Pin ESP32 with wide format (only access to one side of pins on a breadboard) based on Stephen Lilley's HiLetgo ESP-WROOM-32 ESP32 ESP-32S Development Board.
