# Fritzing sketch Putri_RAHMA (saved by Fritzing 0.9.3b)
breadboards: 1

parts:
  ARDUINO_UNO = Arduino Uno (Rev3)
  LCD_+_I2C = LCD screen 16x2 IIC [part_number=101290]
  NodeMCU_ESP8266 = ESP8266 NodeMCU LoLin module
  RELAY = Keyes Relay [package=THT]
  POWER_SUPPLY = Battery
  POMPA_AIR_MINI = water pump/motor  # not connected
  M2 = DFRobot-PH-sensor_in_bb_1
  ULTRASONIK = hc-sr04

nets:
  N1: ARDUINO_UNO.A0, M2.connector0
  N2: ARDUINO_UNO.A4/SDA, LCD_+_I2C.SDA
  N3: ARDUINO_UNO.A5/SCL, LCD_+_I2C.SCL
  N4: ARDUINO_UNO.D8, ULTRASONIK.Echo
  N5: ARDUINO_UNO.D9_PWM, ULTRASONIK.Trig
  N6: ARDUINO_UNO.D10_PWM/SS, NodeMCU_ESP8266.D2
  N7: ARDUINO_UNO.D11_PWM/MOSI, NodeMCU_ESP8266.D1
  N8: ARDUINO_UNO.D7, RELAY.signal
  VCC: ARDUINO_UNO.5V, LCD_+_I2C.VCC, RELAY.power, M2.connector1, ULTRASONIK.VCC
  GND: ARDUINO_UNO.GND, LCD_+_I2C.GND, RELAY.ground, M2.connector2, ULTRASONIK.GND
  N9: RELAY.C, POWER_SUPPLY.+

custom parts:
  LCD screen 16x2 IIC: LCD screen with HD44780 controller enables showing text, symbols, value or anything else that comes from Croduino/Arduino. It is capable of showing 16 symbols in two lines and therefore can be used in many projects that need to send clearly visible and legible output information.. • Color of symbols: White • Backlight: Blue • Dimensions: 80 x 36 x 12 mm • Screen dimensions: 64.5 x 16 mm •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
  ESP8266 NodeMCU LoLin module: ESP8266 based NodeMCU
  Keyes Relay: The Keyes 5V relay module is suitable for SCM development, home appliance control. It uses a 5V~12V TIL control signal which can control DC / AC signal.
  water pump/motor: WATER PUMP BY ARDUBLOCKTR
