# Fritzing sketch Salimah (saved by Fritzing 0.9.3b)
breadboards: 1

parts:
  U1 = ESP8266 NodeMCU LoLin module
  J1 = Piezo Speaker
  LED1 = LED - 5mm [color="Red (633nm)" package="5 mm [THT]"]
  LED2 = LEDs [package=led10mm]
  SW-1 = Vibration sensor module

nets:
  N1: U1.D2, SW-1.Digital_output
  3V3: U1.3V3, SW-1.vcc
  N2: U1.GND, J1.pin1, LED1.cathode, LED2.C, SW-1.Ground
  N3: U1.D6, LED2.A
  N4: U1.D7, J1.pin2
  N5: U1.D8, LED1.anode

custom parts:
  ESP8266 NodeMCU LoLin module: ESP8266 based NodeMCU
  Vibration sensor module: Single-roller type full induction trigger switch. When no vibration or tilt, the product is ON conduction state, and in the steady state, when a vibration or tilt, the switch will be rendered instantly disconnect the conductive resistance increases, generating a current pulse signal, thereby triggering circuit. The default state of the swith is close Digital output Supply voltage:3.3V-5V On-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
