# Fritzing sketch Untitled Sketch (saved by Fritzing 0.9.3b)
breadboards: 1

parts:
  Part1 = Arduino Uno (Rev3)
  부품3 = FC-28 Soil Hygrometer Module
  부품4 = FC-28 Soil Hygrometer Module - Probe
  부품5 = FC-28 Soil Hygrometer Module
  부품6 = FC-28 Soil Hygrometer Module - Probe
  부품7 = FC-28 Soil Hygrometer Module
  부품8 = FC-28 Soil Hygrometer Module - Probe
  J1 = DHT22 temperature-humidity sensor [form="♂ (male)" package=THT]
  KY-1 = Keyes Relay [package=THT]
  WATER_PUMP1 = water pump/motor  # not connected
  VCC1 = Battery

nets:
  N1: Part1.D8, J1.OUT
  N2: Part1.D2, 부품3.DO
  N3: Part1.D3_PWM, 부품5.DO
  N4: Part1.D4, 부품7.DO
  N5: Part1.D7, KY-1.signal
  VCC: Part1.5V, 부품3.VCC, J1.VCC, KY-1.power
  GND: Part1.GND, 부품3.GND, J1.GND, KY-1.ground
  N6: 부품3.POS, 부품4.POS
  N7: 부품3.NEG, 부품4.NEG
  N8: 부품5.POS, 부품6.POS
  N9: 부품5.NEG, 부품6.NEG
  N10: 부품7.POS, 부품8.POS
  N11: 부품7.NEG, 부품8.NEG
  N12: KY-1.NO, VCC1.+

custom parts:
  FC-28 Soil Hygrometer Module: The FC-28 is a soil hygrometer module that uses the Texas Instruments LM393 comparator chip to provide an analog measurement of soil humidity. The digital output is high when soil moisture is over a certain threshold, as determined by adjusting the potentiometer.
  FC-28 Soil Hygrometer Module - Probe: The FC-28 is a soil hygrometer module that uses the Texas Instruments LM393 comparator chip to provide an analog measurement of soil humidity.
  DHT22 temperature-humidity sensor: The DHT22 is a basic, low-cost digital temperature and humidity sensor. It uses a capacitive humidity sensor and a thermistor to measure the surrounding air, and spits out a digital signal on the data pin (no analog input pins needed). It's fairly simple to use, but requires careful timing to grab data. The only real downside of this sensor is you can only get new data from it once every 2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
  Keyes Relay: The Keyes 5V relay module is suitable for SCM development, home appliance control. It uses a 5V~12V TIL control signal which can control DC / AC signal.
  water pump/motor: WATER PUMP BY ARDUBLOCKTR
  Battery: Your standard 2x 18650 battery pack (7,4 Volts)
