# Fritzing sketch rainSensor (saved by Fritzing 0.9.3b)
circuit board: 8.46667cm x 5.64444cm
breadboards: 1

parts:
  Part1 = Arduino Uno (Rev3)
  MOTOR1 = 28BYJ-48 Stepper Motor
  BREAKOUT1 = ULN2003A breakout board
  J1 = DHT22 temperature-humidity sensor [form="♂ (male)" package=THT]
  S1 = LDR light sensor [package=THT]
  YL-83_-_Control_Board1 = YL-83 Rain Sensor - Control Board
  YL-83_-_Detection_Board1 = YL-83 Rain Sensor - Detection Board
  LCD2004-I2C1 = LCD2004-I2C

nets:
  N1: Part1.A0, YL-83_-_Control_Board1.AO
  N2: Part1.A2, S1.pin1
  N3: Part1.A4/SDA, LCD2004-I2C1.SDA
  N4: Part1.A5/SCL, LCD2004-I2C1.SCL
  N5: Part1.D8, BREAKOUT1.In_1
  N6: Part1.D9_PWM, BREAKOUT1.In_2
  N7: Part1.D10_PWM/SS, BREAKOUT1.In_3
  N8: Part1.D11_PWM/MOSI, BREAKOUT1.In_4
  N9: Part1.D2, J1.OUT
  VCC: Part1.5V, BREAKOUT1.+5V, J1.VCC, S1.pin3, YL-83_-_Control_Board1.VCC, LCD2004-I2C1.VCC
  GND: Part1.GND, BREAKOUT1.0V, J1.GND, S1.pin2, YL-83_-_Control_Board1.GND, LCD2004-I2C1.GND
  N10: MOTOR1.BLUE, BREAKOUT1.BLUE_wire
  N11: MOTOR1.PINK, BREAKOUT1.PINK_wire
  N12: MOTOR1.RED, BREAKOUT1.YELLOW_wire
  N13: MOTOR1.ORANGE, BREAKOUT1.ORANGE_wire
  N14: MOTOR1.YELLOW, BREAKOUT1.RED_wire
  N15: YL-83_-_Control_Board1.POS, YL-83_-_Detection_Board1.POS
  N16: YL-83_-_Control_Board1.NEG, YL-83_-_Detection_Board1.NEG

custom parts:
  28BYJ-48 Stepper Motor: 28BYJ-48 gear-reduction stepper motor (small)
  ULN2003A breakout board: ULN2003A 7-way Darlington Transistor Driver on breakoutboard
  DHT22 temperature-humidity sensor: The DHT22 is a basic, low-cost digital temperature and humidity sensor. It uses a capacitive humidity sensor and a thermistor to measure the surrounding air, and spits out a digital signal on the data pin (no analog input pins needed). It's fairly simple to use, but requires careful timing to grab data. The only real downside of this sensor is you can only get new data from it once every 2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
  LDR light sensor: Light sensor module. 3.3 V to 5V power.
  YL-83 Rain Sensor - Control Board: The YL-83 is a rain sensor that has more resistance when dry and less resistance when wet. The module runs at 5V.
  YL-83 Rain Sensor - Detection Board: The YL-83 is a rain sensor that has more resistance when dry and less resistance when wet. The module runs at 5V.
  LCD2004-I2C: A standard character display with 4x20 characters. Comes in many colors with LCM2004 IIC attached.
